// Logisim project 32-bit-single-cycle-processor.circ as structural Verilog
module instruction_memory (
  input  [31:0] Address,
  output [31:0] Instruction
);
endmodule

module alu_control (
  input  [2:0] ALUOp,
  input  [5:0] func,
  output [2:0] ALU_Control
);
endmodule

module main_control (
  input  [5:0] opcode,
  output RegDst,
  output RegWrite,
  output ALUSrc,
  output [2:0] ALUOp,
  output MemRead,
  output MemWrite,
  output MemToReg,
  output bne,
  output beq,
  output j
);

  wire decoder_1_out8, decoder_1_out10, decoder_1_out12, decoder_1_out13, decoder_1_out14, not_1_out;

  not not_1 (not_1_out, opcode[5]);
  Decoder #(.select(5), .disabled(0)) decoder_1 (
    .out0(RegDst), .out2(j), .out4(beq), .out5(bne), .out8(decoder_1_out8), .out10(decoder_1_out10),
    .out12(decoder_1_out12), .out13(decoder_1_out13), .out14(decoder_1_out14), .sel(opcode[4:0]),
    .en(not_1_out));  // open: out1, out3, out6, out7, out9, out11, out15, out16, out17, out18, out19, out20, out21, out22, out23, out24, out25, out26, out27, out28, out29, out30, out31
  Decoder #(.select(5), .disabled(0)) decoder_2 (
    .out3(MemRead), .out11(MemWrite), .sel(opcode[4:0]), .en(opcode[5]));  // open: out0, out1, out2, out4, out5, out6, out7, out8, out9, out10, out12, out13, out14, out15, out16, out17, out18, out19, out20, out21, out22, out23, out24, out25, out26, out27, out28, out29, out30, out31
  nor nor_1 (RegWrite, j, beq, bne, MemWrite);
  nor nor_2 (ALUSrc, decoder_1_out12, decoder_1_out13, decoder_1_out14);
  or or_1 (ALUOp[0], decoder_1_out12, decoder_1_out14, beq, bne);
  or or_2 (ALUOp[1], decoder_1_out13, decoder_1_out14, decoder_1_out10);
  or or_3 (ALUOp[2], decoder_1_out10, decoder_1_out8, MemWrite, MemRead, beq, bne);

  assign MemToReg = MemRead;
endmodule
